// Logisim project DESIGN.circ as structural Verilog: 5 circuits, main circuit main
module main (
  input  A0,
  input  A1,
  input  A2,
  input  A3,
  input  B0,
  input  B1,
  input  B2,
  input  B3,
  input  R
);

  wire adder_4_bits_1_s0, adder_4_bits_1_s1, adder_4_bits_1_s2, adder_4_bits_1_s3, seven_segment_decoder_1_a,
       seven_segment_decoder_1_b, seven_segment_decoder_1_c, seven_segment_decoder_1_d,
       seven_segment_decoder_1_e, seven_segment_decoder_1_f, seven_segment_decoder_1_g,
       seven_segment_decoder_2_a, seven_segment_decoder_2_b, seven_segment_decoder_2_c,
       seven_segment_decoder_2_d, seven_segment_decoder_2_e, seven_segment_decoder_2_f,
       seven_segment_decoder_2_g, seven_segment_decoder_3_a, seven_segment_decoder_3_b,
       seven_segment_decoder_3_c, seven_segment_decoder_3_d, seven_segment_decoder_3_e,
       seven_segment_decoder_3_f, seven_segment_decoder_3_g, xor_1_out, xor_2_out, xor_3_out, xor_4_out;

  xor xor_1 (xor_1_out, B0, R);
  xor xor_2 (xor_2_out, B1, R);
  xor xor_3 (xor_3_out, B2, R);
  xor xor_4 (xor_4_out, B3, R);
  Seven_segment_decoder seven_segment_decoder_1 (
    .D1(A0), .D0(A1), .D2(A2), .D3(A3), .A(seven_segment_decoder_1_a), .B(seven_segment_decoder_1_b),
    .C(seven_segment_decoder_1_c), .D(seven_segment_decoder_1_d), .E(seven_segment_decoder_1_e),
    .F(seven_segment_decoder_1_f), .G(seven_segment_decoder_1_g));
  Adder_4_Bits adder_4_bits_1 (
    .C_in(R), .A0(A0), .B0(xor_1_out), .A1(A1), .B1(xor_2_out), .A2(A2), .B2(xor_3_out), .A3(A3),
    .B3(xor_4_out), .S0(adder_4_bits_1_s0), .S1(adder_4_bits_1_s1), .S2(adder_4_bits_1_s2),
    .S3(adder_4_bits_1_s3));  // open: C_out
  Seven_segment_decoder seven_segment_decoder_2 (
    .D1(B0), .D0(B1), .D2(B2), .D3(B3), .A(seven_segment_decoder_2_a), .B(seven_segment_decoder_2_b),
    .C(seven_segment_decoder_2_c), .D(seven_segment_decoder_2_d), .E(seven_segment_decoder_2_e),
    .F(seven_segment_decoder_2_f), .G(seven_segment_decoder_2_g));
  _7_Segment_Display #(.decimalPoint("false")) u_7_segment_display_1 (
    .g(seven_segment_decoder_1_g), .f(seven_segment_decoder_1_f), .a(seven_segment_decoder_1_a),
    .b(seven_segment_decoder_1_b), .e(seven_segment_decoder_1_e), .d(seven_segment_decoder_1_d),
    .c(seven_segment_decoder_1_c));
  _7_Segment_Display #(.decimalPoint("false")) u_7_segment_display_2 (
    .g(seven_segment_decoder_2_g), .f(seven_segment_decoder_2_f), .a(seven_segment_decoder_2_a),
    .b(seven_segment_decoder_2_b), .e(seven_segment_decoder_2_e), .d(seven_segment_decoder_2_d),
    .c(seven_segment_decoder_2_c));
  Seven_segment_decoder seven_segment_decoder_3 (
    .D1(adder_4_bits_1_s0), .D0(adder_4_bits_1_s1), .D2(adder_4_bits_1_s2), .D3(adder_4_bits_1_s3),
    .A(seven_segment_decoder_3_a), .B(seven_segment_decoder_3_b), .C(seven_segment_decoder_3_c),
    .D(seven_segment_decoder_3_d), .E(seven_segment_decoder_3_e), .F(seven_segment_decoder_3_f),
    .G(seven_segment_decoder_3_g));
  _7_Segment_Display #(.decimalPoint("false")) u_7_segment_display_3 (
    .g(seven_segment_decoder_3_g), .f(seven_segment_decoder_3_f), .a(seven_segment_decoder_3_a),
    .b(seven_segment_decoder_3_b), .e(seven_segment_decoder_3_e), .d(seven_segment_decoder_3_d),
    .c(seven_segment_decoder_3_c));
endmodule

module HA (
  input  X,
  input  Y,
  output S,
  output C
);

  xor xor_1 (S, X, Y);
  and and_1 (C, X, Y);
endmodule

module FA (
  input  cin,
  input  a,
  input  b,
  output s,
  output c
);

  wire ha_1_c, ha_1_s, ha_2_c;

  HA ha_1 (.X(a), .Y(b), .S(ha_1_s), .C(ha_1_c));
  or or_1 (c, ha_2_c, ha_1_c);
  HA ha_2 (.X(ha_1_s), .Y(cin), .S(s), .C(ha_2_c));
endmodule

module Adder_4_Bits (
  input  C_in,
  input  A0,
  input  B0,
  input  A1,
  input  B1,
  input  A2,
  input  B2,
  input  A3,
  input  B3,
  output S0,
  output S1,
  output S2,
  output S3,
  output C_out
);

  wire fa_1_c, fa_2_c, fa_3_c;

  FA fa_1 (.cin(C_in), .a(A0), .b(B0), .s(S0), .c(fa_1_c));
  FA fa_2 (.cin(fa_1_c), .a(A1), .b(B1), .s(S1), .c(fa_2_c));
  FA fa_3 (.cin(fa_2_c), .a(A2), .b(B2), .s(S2), .c(fa_3_c));
  FA fa_4 (.cin(fa_3_c), .a(A3), .b(B3), .s(S3), .c(C_out));
endmodule

module Seven_segment_decoder (
  input  D1,
  input  D0,
  input  D2,
  input  D3,
  output A,
  output B,
  output C,
  output D,
  output E,
  output F,
  output G
);

  wire and_1_out, and_2_out, and_3_out, and_4_out, and_5_out, and_6_out, and_7_out, and_8_out, and_9_out,
       and_10_out, and_11_out, and_12_out, and_13_out, and_14_out, and_15_out, and_16_out, and_17_out,
       not_1_out, not_2_out, not_3_out, not_4_out;

  not not_1 (not_1_out, D2);
  not not_2 (not_2_out, D3);
  not not_3 (not_3_out, D1);
  not not_4 (not_4_out, D0);
  and and_1 (and_1_out, not_1_out, not_4_out);
  and and_2 (and_2_out, D2, D0);
  and and_3 (and_3_out, D1, D0);
  and and_4 (and_4_out, not_3_out, not_4_out);
  and and_5 (and_5_out, D2, not_3_out, D0);
  and and_6 (and_6_out, not_1_out, not_4_out);
  and and_7 (and_7_out, D1, not_4_out);
  and and_8 (and_8_out, not_1_out, D1);
  and and_9 (and_9_out, not_4_out, D1);
  and and_10 (and_10_out, not_1_out, not_4_out);
  and and_11 (and_11_out, not_3_out, not_4_out);
  and and_12 (and_12_out, D2, not_3_out);
  and and_13 (and_13_out, D2, not_4_out);
  and and_14 (and_14_out, D2, not_4_out);
  and and_15 (and_15_out, D2, not_3_out);
  and and_16 (and_16_out, D1, not_4_out);
  and and_17 (and_17_out, not_1_out, D1);
  or or_1 (A, D3, D1, and_1_out, and_2_out);
  or or_2 (B, not_1_out, and_3_out, and_4_out);
  or or_3 (C, not_3_out, D0, D2);
  or or_4 (D, and_5_out, and_6_out, and_7_out, and_8_out, D3);
  or or_5 (E, and_9_out, and_10_out);
  or or_6 (F, D3, and_11_out, and_12_out, and_13_out);
  or or_7 (G, D3, and_14_out, and_15_out, and_16_out, and_17_out);
endmodule
